# Fritzing sketch NeoPixel_simple-DEL177 (saved by Fritzing 1.0.2b)
breadboards: 2

parts:
  U4 = ESP 32 DEVKIT DOIT  # not connected
  R3 = Resistor [tolerance=±5% resistance=220 package="1206 [SMD]"]
  LED2 = smd LED [color="Red (633nm)" package="1206 [SMD]"]
  Mod1 = KY-018 Photoresistor Module [package="Breakout board"]  # not connected
  U5 = WS2812 RGB LED strip

nets:
  N1: R3.Pin_0, LED2.anode
  N2: LED2.cathode, U5.GND

custom parts:
  KY-018 Photoresistor Module: KY-018 Photoresistor module, used to measure light intensity. It can determine the presence or absence of light.
  WS2812 RGB LED strip: WS2812 strip
