# Fritzing sketch NeoPixel_simple (saved by Fritzing 1.0.2b)
breadboards: 2

parts:
  MH-ET_LIVE_ESP32_DEVKIT1 = MH-ET LIVE ESP32 DEVKIT 38 pins
  U1 = WS2812 RGB LED strip

nets:
  N1: MH-ET_LIVE_ESP32_DEVKIT1.IO12, U1.DIN
  GND: MH-ET_LIVE_ESP32_DEVKIT1.GND, U1.GND
  5V: MH-ET_LIVE_ESP32_DEVKIT1.5V, U1.VCC

custom parts:
  MH-ET LIVE ESP32 DEVKIT 38 pins: http://mh.nodebb.com/topic/2/mh-et-live-esp32-devkit
  WS2812 RGB LED strip: WS2812 strip
